# Fritzing sketch 1.BotonGrandeEnVivo (saved by Fritzing 1.0.1rc)
breadboards: 1

parts:
  WeMos_D1_Mini1 = WeMos D1 Mini
  Relay_5V3 = Keyes Relay [package=THT]
  R1 = Resistor [tolerance=±5% power=0.25W resistance=330 package=THT]
  S1 = Pushbutton [package="[THT]"]
  LED1 = LED - 5mm [color="Red (633nm)" current=0.030A package="5 mm [THT]"]
  Relay_5V4 = Keyes Relay [package=THT]
  S2 = Pushbutton [package="[THT]"]
  LED2 = LED - 5mm [color="Red (633nm)" current=0.030A package="5 mm [THT]"]
  R2 = Resistor [tolerance=±5% power=0.25W resistance=330 package=THT]
  LED3 = LED - 5mm [color="Red (633nm)" current=0.030A package="5 mm [THT]"]
  LED4 = LED - 5mm [color="Blue (525nm)" current=0.030A package="5 mm [THT]"]
  R3 = Resistor [tolerance=±5% power=0.25W resistance=10k package=THT]
  R4 = Resistor [tolerance=±5% power=0.25W resistance=10k package=THT]
  Power_plug2 = Power plug
  U1 = Mini-360 DC-DC Buck converter [package=THT]

nets:
  N1: WeMos_D1_Mini1.3V3, R3.Pin_1, R4.Pin_1
  N2: WeMos_D1_Mini1.5V, Relay_5V3.power, Relay_5V4.power, U1.OUT+
  N3: WeMos_D1_Mini1.D0, Relay_5V4.signal
  N4: WeMos_D1_Mini1.D3, LED2.cathode, R2.Pin_0
  N5: WeMos_D1_Mini1.D4, R1.Pin_1
  N6: WeMos_D1_Mini1.D5, Relay_5V3.signal
  N7: WeMos_D1_Mini1.D7, S2.Pin_3, S2.Pin_4, R3.Pin_0
  N8: WeMos_D1_Mini1.D8, S1.Pin_3, S1.Pin_4, R4.Pin_0
  N9: WeMos_D1_Mini1.G, Relay_5V3.ground, Relay_5V4.ground, U1.OUT-
  N10: Relay_5V3.C, Relay_5V4.C, Power_plug2.GND, U1.IN-
  N11: Relay_5V3.NO, LED4.anode
  N12: R1.Pin_0, LED1.cathode
  N13: S1.Pin_1, S1.Pin_2, LED1.anode, S2.Pin_1, S2.Pin_2, LED2.anode
  N14: Relay_5V4.NO, LED3.anode
  N15: LED3.cathode, LED4.cathode, Power_plug2.VCC, U1.IN+

notes:
  12V

custom parts:
  Keyes Relay: The Keyes 5V relay module is suitable for SCM development, home appliance control. It uses a 5V~12V TIL control signal which can control DC / AC signal.
  Mini-360 DC-DC Buck converter: Mini-360 DC-DC Buck converter. Tiny buck step down voltage converter, input voltage 4.75 to 23V output 1 to 17V adjustable. Available from ebay and the like.
