# Fritzing sketch AlertaOBS (saved by Fritzing 0.9.9b)
breadboards: 1

parts:
  U1 = NodeMCU V1.0
  R1 = Resistor [tolerance=±5% power=0.25 resistance=3330 package=THT]
  R2 = Resistor [tolerance=±5% power=0.25 resistance=330 package=THT]
  S1 = Pushbutton [package="[THT]"]
  S2 = Pushbutton [package="[THT]"]
  LED1 = LED - 5mm [color="Green (570nm)" current=0.030 package="5 mm [THT]"]
  LED2 = LED - 5mm [color="Red (633nm)" current=0.030 package="5 mm [THT]"]
  R3 = Resistor [tolerance=±5% power=0.25 resistance=330 package=THT]
  R4 = Resistor [tolerance=±5% power=0.25 resistance=330 package=THT]
  LED3 = LED - 5mm [color="Yellow (592nm)" current=0.030 package="5 mm [THT]"]
  LED4 = LED - 5mm [color="Blue (525nm)" current=0.030 package="5 mm [THT]"]
  R5 = Resistor [tolerance=±5% power=0.25 resistance=10k package=THT]
  R6 = Resistor [tolerance=±5% power=0.25 resistance=10k package=THT]
  J1 = Piezo Speaker

nets:
  N1: U1.D0, LED1.cathode
  N2: U1.D2, J1.pin2
  N3: U1.D3, LED4.cathode
  N4: U1.D4, LED3.cathode
  N5: U1.3V3, R5.Pin_0, R6.Pin_0
  N6: U1.GND, R1.Pin_1, R2.Pin_1, S1.Pin_3, S1.Pin_4, S2.Pin_3, S2.Pin_4, R3.Pin_1, R4.Pin_1, J1.pin1
  N7: U1.D5, LED2.cathode
  N8: U1.D6, S2.Pin_1, S2.Pin_2, R5.Pin_1
  N9: U1.D7, S1.Pin_1, S1.Pin_2, R6.Pin_1
  N10: R1.Pin_0, LED3.anode
  N11: R2.Pin_0, LED4.anode
  N12: LED1.anode, R4.Pin_0
  N13: LED2.anode, R3.Pin_0

custom parts:
  NodeMCU V1.0: ESP8266 based NodeMCU
