# Fritzing sketch Caja_Diagrama_Rele_Raro (saved by Fritzing 0.9.9b)
breadboards: 3

parts:
  U1 = Mini-360 DC-DC Buck converter [package=THT]
  J1 = 120V duplex outlet_1
  J2 = 220v plug
  J3 = 120V duplex outlet_1
  WeMos_D1_Mini1 = WeMos D1 Mini
  KY-1 = Keyes Relay [package=THT]
  KY-2 = Keyes Relay [package=THT]
  KY-3 = Keyes Relay [package=THT]
  LED1 = LED - 5mm [color="Red (633nm)" current=0.030 package="5 mm [THT]"]
  R1 = Resistor [tolerance=±5% power=0.25 resistance=330 package=THT]
  S1 = Pushbutton [package="[THT]"]
  R2 = Resistor [tolerance=±5% power=0.25 resistance=10k package=THT]
  U2 = Mini-360 DC-DC Buck converter [package=THT]
  J4 = 120V duplex outlet_1
  J6 = 220v plug
  KY-4 = Keyes Relay [package=THT]
  KY-5 = Keyes Relay [package=THT]
  LED2 = LED - 5mm [color="Red (633nm)" current=0.030 package="5 mm [THT]"]
  R3 = Resistor [tolerance=±5% power=0.25 resistance=330 package=THT]
  R4 = Resistor [tolerance=±5% power=0.25 resistance=10k package=THT]
  S2 = Pushbutton [package="[THT]"]
  M1 = DOIT Esp32 DevKit v1 (30 pins long, 11 pins width) [part_number=ESP32S-PIN30]
  Q2 = NPN-Transistor [package="TO92 [THT]"]
  Q3 = NPN-Transistor [package="TO92 [THT]"]
  Q4 = NPN-Transistor [package="TO92 [THT]"]
  R5 = Resistor [tolerance=±5% power=0.25 resistance=330 package=THT]
  R6 = Resistor [tolerance=±5% power=0.25 resistance=10k package=THT]
  R7 = Resistor [tolerance=±5% power=0.25 resistance=330 package=THT]
  R8 = Resistor [tolerance=±5% power=0.25 resistance=10k package=THT]
  R9 = Resistor [tolerance=±5% power=0.25 resistance=330 package=THT]
  R10 = Resistor [tolerance=±5% power=0.25 resistance=10k package=THT]

nets:
  N1: U1.IN-, J1.H1, J1.H2, J2.pin1, J3.H2
  N2: U1.IN+, J2.pin2, KY-1.NO, KY-2.NO, KY-3.NO
  N3: U1.OUT+, WeMos_D1_Mini1.5V, KY-1.power, KY-2.power, KY-3.power, R6.Pin_1, R8.Pin_1, R10.Pin_1
  N4: U1.OUT-, WeMos_D1_Mini1.G, KY-1.ground, KY-2.ground, KY-3.ground, LED1.cathode, S1.Pin_1, S1.Pin_2, Q2.E, Q3.E, Q4.E
  N5: J1.N2, KY-1.C
  N6: J1.N1, KY-2.C
  N7: J3.N2, KY-3.C
  N8: WeMos_D1_Mini1.3V3, R2.Pin_1
  N9: WeMos_D1_Mini1.D1, R5.Pin_1
  N10: WeMos_D1_Mini1.D2, R7.Pin_1
  N11: WeMos_D1_Mini1.D4, R1.Pin_0
  N12: WeMos_D1_Mini1.D8, R9.Pin_1
  N13: WeMos_D1_Mini1.RST, S1.Pin_3, S1.Pin_4, R2.Pin_0
  N14: KY-1.signal, Q3.C, R10.Pin_0
  N15: KY-2.signal, Q2.C, R8.Pin_0
  N16: KY-3.signal, Q4.C, R6.Pin_0
  N17: LED1.anode, R1.Pin_1
  N18: U2.IN-, J4.H1, J4.H2, J6.pin1
  N19: U2.IN+, J6.pin2, KY-4.NO, KY-5.NO
  N20: U2.OUT+, KY-4.power, KY-5.power, M1.VIN
  N21: U2.OUT-, KY-4.ground, KY-5.ground, LED2.cathode, R4.Pin_0, S2.Pin_1, S2.Pin_2, M1.GND
  N22: J4.N2, KY-4.C
  N23: J4.N1, KY-5.C
  N24: KY-4.signal, M1.D4
  N25: KY-5.signal, M1.D5
  N26: LED2.anode, R3.Pin_1
  N27: R3.Pin_0, M1.D2
  N28: R4.Pin_1, S2.Pin_3, S2.Pin_4, M1.EN
  N29: Q2.B, R7.Pin_0
  N30: Q3.B, R9.Pin_0
  N31: Q4.B, R5.Pin_0

notes:
  120V

custom parts:
  Mini-360 DC-DC Buck converter: Mini-360 DC-DC Buck converter. Tiny buck step down voltage converter, input voltage 4.75 to 23V output 1 to 17V adjustable. Available from ebay and the like.
  120V duplex outlet_1: 120V duplex outlet.
  220v plug: Generic 220V AC plug.
  Keyes Relay: The Keyes 5V relay module is suitable for SCM development, home appliance control. It uses a 5V~12V TIL control signal which can control DC / AC signal.
  DOIT Esp32 DevKit v1 (30 pins long, 11 pins width): The DOIT Esp32 DevKit v1 is one of the development board created by DOIT to evaluate the ESP-WROOM-32 module. It is based on the ESP32 microcontroller that boasts Wifi, Bluetooth, Ethernet and Low Power support all in a single chip. (vanepp) made breadboard work, adjusted pin numbering and labels and reduced size of schematic and cleaned up pcb. This chip is 30pins long (2 x15) and 11 pins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
