# Fritzing sketch LucesOBS (saved by Fritzing 0.9.9b)
breadboards: 1
perfboards: 1

parts:
  Relay_5V1 = Keyes Relay [package=THT]
  Relay_5V2 = Keyes Relay [package=THT]
  R1 = Resistor [tolerance=±5% power=0.25 resistance=10k package=THT]
  LED1 = LED - 5mm [color="Blue (505nm)" current=0.030 package="5 mm [THT]"]
  Relay_5V3 = Keyes Relay [package=THT]
  S1 = Pushbutton [package="[THT]"]
  WeMos_D1_Mini1 = WeMos D1 Mini
  WeMos_D1_Mini2 = WeMos D1 Mini
  S2 = Pushbutton [package="[THT]"]
  R2 = Resistor [tolerance=±5% power=0.25 resistance=10k package=THT]
  J1 = female pin header, 2 pins [form="♀ (female)"]  # not connected
  J2 = female pin header, 3 pins [form="♀ (female)"]  # not connected
  J3 = female pin header, 3 pins [form="♀ (female)"]  # not connected
  J4 = female pin header, 3 pins [form="♀ (female)"]  # not connected
  J5 = female pin header, 2 pins [form="♀ (female)"]  # not connected
  J7 = female pin header, 2 pins [form="♀ (female)"]
  J8 = female pin header, 2 pins [form="♀ (female)"]
  J9 = female pin header, 2 pins [form="♀ (female)"]
  Power_plug1 = Power plug
  J10 = female pin header, 2 pins [form="♀ (female)"]
  J11 = female pin header, 2 pins [form="♀ (female)"]

nets:
  N1: Relay_5V1.signal, Relay_5V2.signal, Relay_5V3.signal, WeMos_D1_Mini1.5V, J11.pin2
  N2: Relay_5V1.power, WeMos_D1_Mini1.D1
  N3: Relay_5V1.ground, Relay_5V2.ground, LED1.anode, Relay_5V3.ground, S1.Pin_1, S1.Pin_2, WeMos_D1_Mini1.G, J11.pin1
  N4: Relay_5V1.C, J8.pin1
  N5: Relay_5V1.NO, Relay_5V2.NO, Relay_5V3.NO, Power_plug1.GND, J10.pin1
  N6: Relay_5V2.power, WeMos_D1_Mini1.D8
  N7: Relay_5V2.C, J7.pin1
  N8: R1.Pin_0, LED1.cathode
  N9: R1.Pin_1, WeMos_D1_Mini1.D4
  N10: Relay_5V3.power, WeMos_D1_Mini1.D2
  N11: Relay_5V3.C, J9.pin1
  N12: S1.Pin_3, S1.Pin_4, WeMos_D1_Mini1.RST
  N13: WeMos_D1_Mini2.D4, R2.Pin_0
  N14: S2.Pin_1, S2.Pin_2
  N15: S2.Pin_3, S2.Pin_4
  N16: J7.pin2, J8.pin2, J9.pin2, Power_plug1.VCC, J10.pin2

notes:
  120V
  Tranformador

custom parts:
  Keyes Relay: The Keyes 5V relay module is suitable for SCM development, home appliance control. It uses a 5V~12V TIL control signal which can control DC / AC signal.

// code stored in the sketch: bluetoothLight.ino
char blueToothVal;           //value sent over via bluetooth
char lastValue;              //stores last state of device (on/off)
 
void setup()
{
 Serial.begin(9600); 
 pinMode(13,OUTPUT);
 pinMode(12,INPUT);
}
 
 
void loop()
{
  if(Serial.available())
  {//if there is data being recieved
    blueToothVal=Serial.read(); //read it
  }
  if (blueToothVal=='n')
  {//if value from bluetooth serial is n
    digitalWrite(13,HIGH);            //switch on LED
    if (lastValue!='n')
      Serial.println(F("LED is on")); //print LED is on
    lastValue=blueToothVal;
  }
  else if (blueToothVal=='f')
  {//if value from bluetooth serial is n
    digitalWrite(13,LOW);             //turn off LED
    if (lastValue!='f')
      Serial.println(F("LED is off")); //print LED is on
    lastValue=blueToothVal;
  }
  delay(250);
}
